// Digital circuit jelly-seven.dig as structural Verilog
module jelly_seven (
  input  clock,
  input  halt,
  input  D0,
  input  D1,
  input  D2,
  input  D3,
  input  D4,
  input  D5,
  input  D6,
  input  D7,
  input  MR8,
  output \begin ,
  output again,
  output D0_2,
  output D1_2,
  output D2_2,
  output D3_2,
  output D4_2,
  output D5_2,
  output D6_2,
  output D7_2,
  output A0,
  output A1,
  output A2,
  output A3,
  output A4,
  output A5,
  output A6,
  output A7
);

  wire and_1_out, not_1_out, not_2_out, pulldown_17_out, pulldown_18_out, pulldown_19_out, pulldown_20_out,
       pulldown_21_out, pulldown_22_out, pulldown_23_out, pulldown_24_out, U4_pin11, U5_pin1, U5_pin11,
       U6_pin1, U6_pin11, U7_pin1, U7_pin11, U7_pin12, U7_pin13, U7_pin14, U7_pin15, U7_pin16, U7_pin17,
       U7_pin18, U7_pin19, U7_pin20, U8_pin1, U8_pin9, U8_pin10, U8_pin14, U8_pin15;
  wire [2:0] U1_p11, U1_p13, U2_p10, U3_p15;
  wire [7:0] U4_pin6, U4_pin18, U5_pin3, U5_pin6;
  wire [7:5] U1_p21, U2_p22;

  LED led_1 (.in(clock));
  not not_1 (not_1_out, halt);
  LED led_2 (.in(not_1_out));
  and and_1 (and_1_out, clock, not_1_out);
  not not_2 (not_2_out, U8_pin14);
  _74193 U8 (
    .pin1(U8_pin1), .pin2(U4_pin6[0]), .pin3(U4_pin6[1]), .pin4(1'b0), .pin5(and_1_out), .pin6(U4_pin6[2]),
    .pin7(U4_pin6[3]), .pin8(1'b0), .pin9(U8_pin9), .pin10(U8_pin10), .pin11(1'b1), .pin14(U8_pin14),
    .pin15(U8_pin15), .pin16(1'b1));  // open: pin12, pin13
  _74273 U4 (
    .pin1(not_2_out), .pin2(U4_pin6[4]), .pin3(U4_pin18[0]), .pin4(U4_pin18[1]), .pin5(U4_pin6[5]),
    .pin6(U4_pin6[6]), .pin7(U4_pin18[2]), .pin8(U4_pin18[3]), .pin9(U4_pin6[7]), .pin10(1'b0),
    .pin11(U4_pin11), .pin12(U8_pin15), .pin13(U4_pin18[4]), .pin14(U4_pin18[5]), .pin15(U8_pin1),
    .pin16(U8_pin10), .pin17(U4_pin18[6]), .pin18(U4_pin18[7]), .pin19(U8_pin9), .pin20(1'b1));
  _74273 U5 (
    .pin1(U5_pin1), .pin2(U5_pin6[0]), .pin3(U5_pin3[0]), .pin4(U5_pin3[1]), .pin5(U5_pin6[1]),
    .pin6(U5_pin6[2]), .pin7(U5_pin3[2]), .pin8(U5_pin3[3]), .pin9(U5_pin6[3]), .pin10(1'b0),
    .pin11(U5_pin11), .pin12(U5_pin6[4]), .pin13(U5_pin3[4]), .pin14(U5_pin3[5]), .pin15(U5_pin6[5]),
    .pin16(U5_pin6[6]), .pin17(U5_pin3[6]), .pin18(U5_pin3[7]), .pin19(U5_pin6[7]), .pin20(1'b1));
  // _28c16 U1: pin names not known; wires that end beside it: U4_pin6[7], U4_pin6[6], U4_pin6[5], U4_pin6[4], U4_pin6[3], U4_pin6[2], U4_pin6[1], U4_pin6[0], U1_p11[0], U1_p11[1], U1_p11[2], 1'b1, U1_p13[0], U1_p13[1], 1'b1, 1'b0, U1_p13[2], 1'b0, U1_p21[7], U1_p21[6], U1_p21[5]
  // _28c16 U2: pin names not known; wires that end beside it: 1'b0, U4_pin6[7], U4_pin6[6], U4_pin6[5], U4_pin6[4], U4_pin6[3], U4_pin6[2], U4_pin6[1], U4_pin6[0], U2_p10[0], U2_p10[1], U2_p10[2], 1'b0, 1'b1, U1_p13[0], U1_p13[1], 1'b1, 1'b0, U1_p13[2], 1'b0, U2_p22[7], U2_p22[6], U2_p22[5]
  // _28c16 U3: pin names not known; wires that end beside it: U5_pin1, U5_pin6[7], U5_pin6[6], U5_pin6[5], U5_pin6[4], U5_pin6[3], U5_pin6[2], U5_pin6[1], U5_pin6[0], U4_pin18[0], U4_pin18[1], U4_pin18[2], 1'b0, 1'b1, U3_p15[0], U3_p15[1], 1'b1, 1'b0, U3_p15[2], 1'b0, U4_pin18[7], U4_pin18[6], U4_pin18[5], U3_p15
  _74574 U6 (
    .pin1(U6_pin1), .pin2(U4_pin18[0]), .pin3(U4_pin18[1]), .pin4(U4_pin18[2]), .pin5(U4_pin18[3]),
    .pin6(U4_pin18[4]), .pin7(U4_pin18[5]), .pin8(U4_pin18[6]), .pin9(U4_pin18[7]), .pin10(1'b0),
    .pin11(U6_pin11), .pin12(U5_pin3[7]), .pin13(U5_pin3[6]), .pin14(U5_pin3[5]), .pin15(U5_pin3[4]),
    .pin16(U5_pin3[3]), .pin17(U5_pin3[2]), .pin18(U5_pin3[1]), .pin19(U5_pin3[0]), .pin20(1'b1));
  LED led_3 (.in(D0_2));
  PullDown pulldown_1 (.out(D0_2));
  LED led_4 (.in(A0));
  PullDown pulldown_2 (.out(A0));
  LED led_5 (.in(D2_2));
  LED led_6 (.in(D1_2));
  PullDown pulldown_3 (.out(D1_2));
  PullDown pulldown_4 (.out(D2_2));
  LED led_7 (.in(A2));
  LED led_8 (.in(A1));
  PullDown pulldown_5 (.out(A1));
  PullDown pulldown_6 (.out(A2));
  LED led_9 (.in(D4_2));
  LED led_10 (.in(D3_2));
  PullDown pulldown_7 (.out(D3_2));
  PullDown pulldown_8 (.out(D4_2));
  LED led_11 (.in(A4));
  LED led_12 (.in(A3));
  PullDown pulldown_9 (.out(A3));
  PullDown pulldown_10 (.out(A4));
  LED led_13 (.in(D6_2));
  LED led_14 (.in(D5_2));
  PullDown pulldown_11 (.out(D5_2));
  PullDown pulldown_12 (.out(D6_2));
  LED led_15 (.in(A6));
  LED led_16 (.in(A5));
  PullDown pulldown_13 (.out(A5));
  PullDown pulldown_14 (.out(A6));
  LED led_17 (.in(D7_2));
  PullDown pulldown_15 (.out(D7_2));
  LED led_18 (.in(A7));
  PullDown pulldown_16 (.out(A7));
  _74245 U7 (
    .pin1(U7_pin1), .pin10(1'b0), .pin11(U7_pin11), .pin12(U7_pin12), .pin13(U7_pin13), .pin14(U7_pin14),
    .pin15(U7_pin15), .pin16(U7_pin16), .pin17(U7_pin17), .pin18(U7_pin18), .pin19(U7_pin19), .pin20(U7_pin20));  // open: pin2, pin3, pin4, pin5, pin6, pin7, pin8, pin9
  LED led_19 (.in(pulldown_18_out));
  LED led_20 (.in(pulldown_17_out));
  PullDown pulldown_17 (.out(pulldown_17_out));
  PullDown pulldown_18 (.out(pulldown_18_out));
  LED led_21 (.in(pulldown_20_out));
  LED led_22 (.in(pulldown_19_out));
  PullDown pulldown_19 (.out(pulldown_19_out));
  PullDown pulldown_20 (.out(pulldown_20_out));
  LED led_23 (.in(pulldown_22_out));
  LED led_24 (.in(pulldown_21_out));
  PullDown pulldown_21 (.out(pulldown_21_out));
  PullDown pulldown_22 (.out(pulldown_22_out));
  LED led_25 (.in(pulldown_24_out));
  LED led_26 (.in(pulldown_23_out));
  PullDown pulldown_23 (.out(pulldown_23_out));
  PullDown pulldown_24 (.out(pulldown_24_out));

  // Notes on the sheet:
  //   Decoder eeprom, translate a byte from ASCII into a valid BF instruction, ignores non valid;
  //   Code control eeprom, does  control logic of finite states for execute the current instruction;
  //   Tape control eeprom, selects which tape is active for use the Data bus and defines modes;
  //   Math operator eeprom, perform all math operations as table lookups;
  //   Data Bus
  //   Basic Logic Level,
  //   check for fail states,
  //   does hold for swap tapes
  //   does hold for move direction
  //   could halt
  //   Address Bus
  //   FSM Bus
  //   pipeline counter
  //   opcode counter
  //   tape control eeprom
  //   Data Bus is shared by all tapes
endmodule
